# Fritzing sketch ATmega328P_breadboard (saved by Fritzing 0.9.6b)
breadboards: 1

parts:
  R1 = Resistor [tolerance=±5% resistance=220 package="2512 [SMD]"]
  U1 = atmega328 [package=dip]
  Part1 = Arduino Uno (Rev3)
  C2 = Ceramic Capacitor [capacitance=100nF voltage=35V package="100 mil [THT, multilayer]"]

nets:
  N1: R1.Pin_0, U1.RESET, Part1.D10_PWM/SS, C2.0, C2.1
  VCC: R1.Pin_1, U1.VCC, U1.AVCC, Part1.5V
  GND: U1.GND, Part1.GND
  N2: U1.D11_(PWM), Part1.D11_PWM/MOSI
  N3: U1.D12, Part1.D12/MISO
  N4: U1.D13, Part1.D13/SCK
